# Fritzing sketch Fritzing Sketch Source File (saved by Fritzing 0.9.3b)
breadboards: 1

parts:
  HC-SR04_Sensor_1 = HC-SR04 Ultrasonic Distance Sensor
  Part1 = Arduino Uno (Rev3) - ICSP
  Part2 = HC-SR501 Body Sensor Module
  LED1 = smd LED [color="Red (633nm)" package="1206 [SMD]"]
  R1 = Resistor [tolerance=±5% resistance=220 package="2512 [SMD]"]
  J1 = Piezo Speaker

nets:
  VCC: HC-SR04_Sensor_1.VCC, Part1.5V, Part2.VCC
  N1: HC-SR04_Sensor_1.TRIG, Part1.D13/SCK
  N2: HC-SR04_Sensor_1.ECHO, Part1.ICSP_MISO, Part1.D12/MISO
  GND: HC-SR04_Sensor_1.GND, Part1.GND, Part2.GND, LED1.cathode, R1.Pin_0, J1.pin2
  N3: Part1.D8, J1.pin1
  N4: Part1.D3_PWM, Part2.OUT
  N5: Part1.D4, LED1.anode, R1.Pin_1

notes:
  Developed By Web Dev Fusion
  https://www.webdevfusion.com
  GND - Green
  VCC - Orange
  GPIO - Blue

custom parts:
  HC-SR501 Body Sensor Module: Pyroelectric Infrared PIR Motion Sensor Detector Module
